# Fritzing sketch 74hc595-hardware-circuit (saved by Fritzing 1.0.1rc)
breadboards: 1

parts:
  R1 = Resistor [tolerance=±5% power=0.25W resistance=220 package=THT]  # not connected
  Part1 = Arduino Uno (Rev3)
  U1 = 74HC595 [package="DIP16 [THT]"]
  7_Segment1 = 7 Segment Display
  R2 = Resistor [tolerance=±5% power=0.25W resistance=330 package=THT]

nets:
  N1: Part1.D10_PWM/SS, U1.ST_CP
  N2: Part1.D11_PWM/MOSI, U1.DS
  N3: Part1.D13/SCK, U1.SH_CP
  5V: Part1.5V, U1.MR, U1.VCC
  GND: Part1.GND, U1.GND, U1.OE, R2.Pin_0
  N4: U1.Q1, 7_Segment1.Segment_B
  N5: U1.Q2, 7_Segment1.Segment_C
  N6: U1.Q3, 7_Segment1.Segment_D
  N7: U1.Q4, 7_Segment1.Segment_E
  N8: U1.Q5, 7_Segment1.Segment_F
  N9: U1.Q6, 7_Segment1.Segment_G
  N10: U1.Q7, 7_Segment1.Segment_DP
  N11: U1.Q0, 7_Segment1.Segment_A
  N12: 7_Segment1.common_cathode, R2.Pin_1
