# Fritzing sketch led-matrix-circuit (saved by Fritzing 1.0.1rc)
breadboards: 2

parts:
  Part1 = Arduino Uno (Rev3)
  Disp1 = 38mm 8x8 dot matrix column cathode led display with narrow pcb pads
  R1 = Resistor [tolerance=±5% power=0.25W resistance=330 package=THT]
  R2 = Resistor [tolerance=±5% power=0.25W resistance=330 package=THT]
  R3 = Resistor [tolerance=±5% power=0.25W resistance=330 package=THT]
  R4 = Resistor [tolerance=±5% power=0.25W resistance=330 package=THT]
  R5 = Resistor [tolerance=±5% power=0.25W resistance=330 package=THT]
  R6 = Resistor [tolerance=±5% power=0.25W resistance=330 package=THT]
  R7 = Resistor [tolerance=±5% power=0.25W resistance=330 package=THT]
  R8 = Resistor [tolerance=±5% power=0.25W resistance=330 package=THT]

nets:
  N1: Part1.A0, Disp1.pin_13
  N2: Part1.A1, R8.Pin_1
  N3: Part1.A2, Disp1.pin_15
  N4: Part1.A3, Disp1.pin_16
  N5: Part1.D8, R4.Pin_0
  N6: Part1.D9_PWM, R5.Pin_0
  N7: Part1.D10_PWM/SS, R6.Pin_1
  N8: Part1.D11_PWM/MOSI, Disp1.pin_10
  N9: Part1.D12/MISO, Disp1.pin_11
  N10: Part1.D13/SCK, R7.Pin_1
  N11: Part1.D2, R1.Pin_0
  N12: Part1.D3_PWM, R2.Pin_0
  N13: Part1.D6_PWM, R3.Pin_0
  N14: Disp1.pin_9, R6.Pin_0
  N15: Disp1.pin_12, R7.Pin_0
  N16: Disp1.pin_14, R8.Pin_0
