# Fritzing sketch max7219-breadboard-circuit (saved by Fritzing 1.0.1rc)
breadboards: 2

parts:
  Disp1 = 38mm 8x8 dot matrix column cathode led display with narrow pcb pads
  U1 = MAX7219 [package=dil24]
  Part1 = Arduino Uno (Rev3)
  R1 = Resistor [tolerance=±5% power=0.25W resistance=10k package=THT]

nets:
  N1: Disp1.pin_1, U1.DIG4
  N2: Disp1.pin_2, U1.DIG6
  N3: Disp1.pin_3, U1.SEGA
  N4: Disp1.pin_4, U1.SEGB
  N5: Disp1.pin_5, U1.DIG7
  N6: Disp1.pin_6, U1.SEGD
  N7: Disp1.pin_7, U1.DIG5
  N8: Disp1.pin_8, U1.DIG2
  N9: Disp1.pin_9, U1.DIG0
  N10: Disp1.pin_10, U1.SEGC
  N11: Disp1.pin_11, U1.SEGE
  N12: Disp1.pin_12, U1.DIG3
  N13: Disp1.pin_13, U1.SEGDP
  N14: Disp1.pin_14, U1.DIG1
  N15: Disp1.pin_15, U1.SEGF
  N16: Disp1.pin_16, U1.SEGG
  N17: U1.DIN, Part1.D11_PWM/MOSI
  GND: U1.GND, U1.GND2, Part1.GND
  N18: U1.LOAD, Part1.D10_PWM/SS
  N19: U1.CLK, Part1.D13/SCK
  N20: U1.ISET, R1.Pin_0
  VCC: U1.VCC, Part1.5V, R1.Pin_1
