# Fritzing sketch shift-register-daisy-chain (saved by Fritzing 1.0.1rc)
breadboards: 1

parts:
  Part1 = Arduino Uno (Rev3)
  7_Segment1 = 7 Segment Display
  7_Segment2 = 7 Segment Display
  U1 = 74HC595 [package="DIP16 [THT]"]
  U2 = 74HC595 [package="DIP16 [THT]"]
  R1 = Resistor [tolerance=±5% power=0.25W resistance=330 package=THT]
  R2 = Resistor [tolerance=±5% power=0.25W resistance=330 package=THT]

nets:
  N1: Part1.D10_PWM/SS, U1.ST_CP, U2.ST_CP
  N2: Part1.D11_PWM/MOSI, U1.DS
  N3: Part1.D13/SCK, U1.SH_CP, U2.SH_CP
  VCC: Part1.5V, U1.MR, U1.VCC, U2.MR, U2.VCC
  GND: Part1.GND, U1.GND, U1.OE, U2.GND, R1.Pin_0, R2.Pin_0
  N4: 7_Segment1.Segment_E, U1.Q4
  N5: 7_Segment1.Segment_D, U1.Q3
  N6: 7_Segment1.common_cathode, R1.Pin_1
  N7: 7_Segment1.Segment_C, U1.Q2
  N8: 7_Segment1.Segment_B, U1.Q1
  N9: 7_Segment1.Segment_A, U1.Q0
  N10: 7_Segment1.Segment_F, U1.Q5
  N11: 7_Segment1.Segment_G, U1.Q6
  N12: 7_Segment2.Segment_E, U2.Q4
  N13: 7_Segment2.Segment_D, U2.Q3
  N14: 7_Segment2.common_cathode, R2.Pin_1
  N15: 7_Segment2.Segment_C, U2.Q2
  N16: 7_Segment2.Segment_B, U2.Q1
  N17: 7_Segment2.Segment_A, U2.Q0
  N18: 7_Segment2.Segment_F, U2.Q5
  N19: 7_Segment2.Segment_G, U2.Q6
  N20: U1.Q7', U2.DS
