# Fritzing sketch circuit (saved by Fritzing 1.0.1rc)
breadboards: 1

parts:
  C1 = Electrolytic Capacitor [capacitance=1µF voltage=35V package="100 mil [THT, electrolytic]"]
  Part1 = Arduino Uno (Rev3)
  LED1 = LED - 5mm [color="Red (633nm)" current=0.030A package="5 mm [THT]"]
  LED2 = LED - 5mm [color="Red (633nm)" current=0.030A package="5 mm [THT]"]
  LED3 = LED - 5mm [color="Red (633nm)" current=0.030A package="5 mm [THT]"]
  LED4 = LED - 5mm [color="Red (633nm)" current=0.030A package="5 mm [THT]"]
  LED5 = LED - 5mm [color="Red (633nm)" current=0.030A package="5 mm [THT]"]
  LED6 = LED - 5mm [color="Red (633nm)" current=0.030A package="5 mm [THT]"]
  LED7 = LED - 5mm [color="Red (633nm)" current=0.030A package="5 mm [THT]"]
  LED8 = LED - 5mm [color="Red (633nm)" current=0.030A package="5 mm [THT]"]
  R1 = Resistor [tolerance=±5% power=0.25W resistance=330 package=THT]
  R2 = Resistor [tolerance=±5% power=0.25W resistance=330 package=THT]
  R3 = Resistor [tolerance=±5% power=0.25W resistance=330 package=THT]
  R4 = Resistor [tolerance=±5% power=0.25W resistance=330 package=THT]
  R5 = Resistor [tolerance=±5% power=0.25W resistance=330 package=THT]
  R6 = Resistor [tolerance=±5% power=0.25W resistance=330 package=THT]
  R7 = Resistor [tolerance=±5% power=0.25W resistance=330 package=THT]
  R8 = Resistor [tolerance=±5% power=0.25W resistance=330 package=THT]
  S1 = Pushbutton [package="[THT]"]
  R9 = Resistor [tolerance=±5% power=0.25W resistance=1k package=THT]

nets:
  N1: C1.-, R9.Pin_1
  N2: C1.+, Part1.D2, S1.Pin_1, S1.Pin_2, R9.Pin_0
  N3: Part1.D8, R5.Pin_0
  N4: Part1.D9_PWM, R6.Pin_0
  N5: Part1.D10_PWM/SS, R7.Pin_0
  N6: Part1.D11_PWM/MOSI, R8.Pin_0
  N7: Part1.D4, R1.Pin_0
  N8: Part1.D5_PWM, R2.Pin_0
  N9: Part1.D6_PWM, R3.Pin_0
  N10: Part1.D7, R4.Pin_0
  N11: Part1.5V, S1.Pin_3, S1.Pin_4
  N12: Part1.GND, LED1.cathode, LED2.cathode, LED3.cathode, LED4.cathode, LED5.cathode, LED6.cathode, LED7.cathode, LED8.cathode
  N13: LED1.anode, R1.Pin_1
  N14: LED2.anode, R2.Pin_1
  N15: LED3.anode, R3.Pin_1
  N16: LED4.anode, R4.Pin_1
  N17: LED5.anode, R5.Pin_1
  N18: LED6.anode, R6.Pin_1
  N19: LED7.anode, R7.Pin_1
  N20: LED8.anode, R8.Pin_1
