# Fritzing sketch circuit (saved by Fritzing 1.0.1rc)

parts:
  Part1 = Arduino Nano (Rev3.0)
  A1 = hiletgo-max7219-8digit-led-display_1

nets:
  N1: Part1.D10, A1.connector3
  N2: Part1.D11/MOSI, A1.connector2
  N3: Part1.GND, A1.connector1
  N4: Part1.5V, A1.connector0
  N5: Part1.D13/SCK, A1.connector4
