# Fritzing sketch circuit (saved by Fritzing 1.0.1rc)
breadboards: 1

parts:
  R1 = Resistor [tolerance=±5% power=0.25W resistance=220 package=THT]
  LED1 = LED - 5mm [color="Red (633nm)" current=0.030A package="5 mm [THT]"]
  Part1 = Arduino Uno (Rev3)

nets:
  N1: R1.Pin_0, Part1.D11_PWM/MOSI
  N2: R1.Pin_1, LED1.anode
  N3: LED1.cathode, Part1.GND
