# Fritzing sketch circuit (saved by Fritzing 1.0.1rc)
breadboards: 1

parts:
  Part1 = Arduino Uno (Rev3)
  LED1 = LED - 5mm [color="Red (633nm)" current=0.030A package="5 mm [THT]"]  # not connected
  R2 = Resistor [tolerance=±5% power=0.25W resistance=220 package=THT]
  R4 = 6mm Trimmer Potentiometer [maximum_resistance=10kΩ knob_status=50% power=0.5W package=THT]

nets:
  N1: Part1.A0, R4.wiper
  N2: Part1.GND, R2.Pin_0, R4.leg1, R4.leg2
