# Fritzing sketch circuit (saved by Fritzing 1.0.1rc)
breadboards: 1

parts:
  Part1 = Arduino Uno (Rev3)
  LED1 = LED - 5mm [color="Red (633nm)" current=0.030A package="5 mm [THT]"]
  R1 = Resistor [tolerance=±5% power=0.25W resistance=220 package=THT]
  Button_Down = Pushbutton [package="[THT]"]
  Button_up = Pushbutton [package="[THT]"]

nets:
  N1: Part1.D8, Button_Down.Pin_1, Button_Down.Pin_2
  N2: Part1.D9_PWM, Button_up.Pin_1, Button_up.Pin_2
  N3: Part1.GND, LED1.cathode, Button_Down.Pin_3, Button_Down.Pin_4, Button_up.Pin_3, Button_up.Pin_4
  N4: Part1.D6_PWM, R1.Pin_0
  N5: LED1.anode, R1.Pin_1
