# Fritzing sketch circuit (saved by Fritzing 1.0.1rc)

parts:
  Part1 = Arduino Uno (Rev3)
  8x8_LED_Modul_mit_MAX1 = 8x8 LED Modul mit MAX7219 [package=THT]
  8x8_LED_Modul_mit_MAX2 = 8x8 LED Modul mit MAX7219 [package=THT]
  8x8_LED_Modul_mit_MAX3 = 8x8 LED Modul mit MAX7219 [package=THT]
  8x8_LED_Modul_mit_MAX4 = 8x8 LED Modul mit MAX7219 [package=THT]

nets:
  N1: Part1.D10_PWM/SS, 8x8_LED_Modul_mit_MAX1.CS_Eingang
  N2: Part1.D11_PWM/MOSI, 8x8_LED_Modul_mit_MAX1.DIN_Eingang
  N3: Part1.D13/SCK, 8x8_LED_Modul_mit_MAX1.CLK_Eingang
  N4: Part1.GND, 8x8_LED_Modul_mit_MAX1.GND_Eingang
  N5: Part1.5V, 8x8_LED_Modul_mit_MAX1.VCC_Eingang
  N6: 8x8_LED_Modul_mit_MAX1.VCC_Ausgang, 8x8_LED_Modul_mit_MAX2.VCC_Eingang
  N7: 8x8_LED_Modul_mit_MAX1.GND_Ausgang, 8x8_LED_Modul_mit_MAX2.GND_Eingang
  N8: 8x8_LED_Modul_mit_MAX1.DOUT_Ausgang, 8x8_LED_Modul_mit_MAX2.DIN_Eingang
  N9: 8x8_LED_Modul_mit_MAX1.CS_Ausgang, 8x8_LED_Modul_mit_MAX2.CS_Eingang
  N10: 8x8_LED_Modul_mit_MAX1.CLK_Ausgang, 8x8_LED_Modul_mit_MAX2.CLK_Eingang
  N11: 8x8_LED_Modul_mit_MAX2.VCC_Ausgang, 8x8_LED_Modul_mit_MAX3.VCC_Eingang
  N12: 8x8_LED_Modul_mit_MAX2.GND_Ausgang, 8x8_LED_Modul_mit_MAX3.GND_Eingang
  N13: 8x8_LED_Modul_mit_MAX2.DOUT_Ausgang, 8x8_LED_Modul_mit_MAX3.DIN_Eingang
  N14: 8x8_LED_Modul_mit_MAX2.CS_Ausgang, 8x8_LED_Modul_mit_MAX3.CS_Eingang
  N15: 8x8_LED_Modul_mit_MAX2.CLK_Ausgang, 8x8_LED_Modul_mit_MAX3.CLK_Eingang
  N16: 8x8_LED_Modul_mit_MAX3.VCC_Ausgang, 8x8_LED_Modul_mit_MAX4.VCC_Eingang
  N17: 8x8_LED_Modul_mit_MAX3.GND_Ausgang, 8x8_LED_Modul_mit_MAX4.GND_Eingang
  N18: 8x8_LED_Modul_mit_MAX3.DOUT_Ausgang, 8x8_LED_Modul_mit_MAX4.DIN_Eingang
  N19: 8x8_LED_Modul_mit_MAX3.CS_Ausgang, 8x8_LED_Modul_mit_MAX4.CS_Eingang
  N20: 8x8_LED_Modul_mit_MAX3.CLK_Ausgang, 8x8_LED_Modul_mit_MAX4.CLK_Eingang
