# Fritzing sketch circuit (saved by Fritzing 1.0.1rc)
breadboards: 1

parts:
  Part1 = Arduino Uno (Rev3)
  R1 = Resistor [tolerance=±5% power=0.25W resistance=1k package=THT]
  R2 = Resistor [tolerance=±5% power=0.25W resistance=220 package=THT]
  S1 = Pushbutton [package="[THT]"]

nets:
  N1: Part1.A0, R1.Pin_1, R2.Pin_0
  N2: Part1.D2, S1.Pin_1, S1.Pin_2
  N3: Part1.5V, R1.Pin_0
  N4: Part1.GND, R2.Pin_1, S1.Pin_3, S1.Pin_4
